# Fritzing sketch RDDonkey (saved by Fritzing 0.9.3b)

parts:
  PWM_Capture = Genuino 101
  Alim_via_micro_USB_rpi = USB connector [package=THT]
  PWM_Generator = 16-Channel 12-bit PWM Servo Driver - I2C [part_number=PCA9685]
  Raspberry_Pi = Raspberry Pi 3 [part_number="+Raspberry Camera"]
  Rx-power_(free_ch) = Dagu DGServo 9g header connector (female) [package=THT]
  Rx-ch0 = Dagu DGServo 9g header connector (female) [package=THT]
  Rx-ch1 = Dagu DGServo 9g header connector (female) [package=THT]
  ESC = Dagu DGServo 9g header (male) [package=THT]
  Servo = Dagu DGServo 9g header (male) [package=THT]
  Alim_via_Hub_USB_rpi = USB connector [package=THT]

nets:
  N1: PWM_Capture.D11_PWM/MOSI, Rx-ch1.pulse
  GND: PWM_Capture.GND, Alim_via_micro_USB_rpi.GND, Alim_via_micro_USB_rpi.chassis6, PWM_Generator.GND, Raspberry_Pi.GND, Rx-power_(free_ch).gnd, ESC.gnd, Servo.gnd, Alim_via_Hub_USB_rpi.GND, Alim_via_Hub_USB_rpi.chassis5, Alim_via_Hub_USB_rpi.chassis6
  N2: PWM_Capture.D0/RX, Raspberry_Pi.GPIO14
  N3: PWM_Capture.D1/TX, Raspberry_Pi.GPIO15
  N4: PWM_Capture.D5_PWM, Rx-ch0.pulse
  5V: PWM_Capture.5V, Alim_via_Hub_USB_rpi.5V
  5V_2: Alim_via_micro_USB_rpi.5V, PWM_Generator.VCC, Raspberry_Pi.5V
  VCC: PWM_Generator.PWRIN, Rx-power_(free_ch).Vcc, ESC.Vcc, Servo.Vcc
  N5: PWM_Generator.PWM1, Servo.pulse
  N6: PWM_Generator.PWM0, ESC.pulse
  N7: PWM_Generator.SDA, Raspberry_Pi.GPIO2
  N8: PWM_Generator.SCL, Raspberry_Pi.GPIO3

notes:
  DIY Robocars France, RD Donkey car schematic, 1
  Serial link (115200)
  I2C

custom parts:
  Genuino 101: A learning and development board that delivers the performance and low-power consumption of the Intel® Curie™ Module with the simplicity of Arduino at an entry-level price. It keeps the same robust form factor and peripheral list of the UNO with the addition of onboard Bluetooth LE capabilities and a 6-axis accelerometer/gyro to help you easily expand your creativity into the connected world.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
  16-Channel 12-bit PWM Servo Driver - I2C: You want to make a cool robot, maybe a hexapod walker, or maybe just a piece of art with a lot of moving parts. Or maybe you want to drive a lot of LEDs with precise PWM output. Using only two pins, control 16 free-running PWM outputs! You can even chain up 62 breakouts to control up to 992 PWM outputs.
